// Logisim project add1bit.circ as structural Verilog: 3 circuits, main circuit add1bit
module add1bit (
  input  in_1,
  input  in_2,
  input  in_3,
  output out_4,
  output out_5
);

  wire and_1_out, and_2_out, and_3_out, xor_1_out;

  xor xor_1 (xor_1_out, in_1, in_2);
  and and_1 (and_1_out, in_1, in_2);
  and and_2 (and_2_out, in_1, in_3);
  and and_3 (and_3_out, in_2, in_3);
  or or_1 (out_5, and_1_out, and_2_out, and_3_out);
  xor xor_2 (out_4, xor_1_out, in_3);

  // Notes on the sheet:
  //   Attention, votre version de Logisim
  //   ne contient pas de tracker. Si vous
  //   enregistrez votre projet, toutes les
  //   informations du tracker seront
  //   définitivement effacées.
endmodule

module add4bits (
  input  in_1,
  input  [3:0] in_2,
  input  [3:0] in_3,
  output [3:0] out_4,
  output out_5
);

  wire add1bits_1_c_out, add1bits_2_c_out, add1bits_3_c_out;

  add1bits add1bits_1 (.A(in_2[0]), .B(in_3[0]), .C_in(in_1), .D(out_4[0]), .C_out(add1bits_1_c_out));
  add1bits add1bits_2 (.A(in_2[1]), .B(in_3[1]), .C_in(add1bits_1_c_out), .D(out_4[1]), .C_out(add1bits_2_c_out));
  add1bits add1bits_3 (.A(in_2[2]), .B(in_3[2]), .C_in(add1bits_2_c_out), .D(out_4[2]), .C_out(add1bits_3_c_out));
  add1bits add1bits_4 (.A(in_2[3]), .B(in_3[3]), .C_in(add1bits_3_c_out), .D(out_4[3]), .C_out(out_5));

  // Notes on the sheet:
  //   Attention, votre version de Logisim
  //   ne contient pas de tracker. Si vous
  //   enregistrez votre projet, toutes les
  //   informations du tracker seront
  //   définitivement effacées.
endmodule

module add1bits (
  input  A,
  input  B,
  input  C_in,
  output D,
  output C_out
);

  wire and_1_out, and_2_out, and_3_out, xor_1_out;

  xor xor_1 (xor_1_out, A, B);
  and and_1 (and_1_out, A, B);
  and and_2 (and_2_out, A, C_in);
  and and_3 (and_3_out, B, C_in);
  or or_1 (C_out, and_1_out, and_2_out, and_3_out);
  xor xor_2 (D, xor_1_out, C_in);

  // Notes on the sheet:
  //   Attention, votre version de Logisim
  //   ne contient pas de tracker. Si vous
  //   enregistrez votre projet, toutes les
  //   informations du tracker seront
  //   définitivement effacées.
endmodule
